# Fritzing sketch PepperzGarden (saved by Fritzing 0.8.5b)
breadboards: 1

parts:
  Arduino_2560 = Arduino Mega 2560 (Rev3)  # not connected
  Ethernet_Shield = Arduino Ethernet Shield (Rev3)
  R3 = Resistor [tolerance=±5% resistance=10k package=THT]
  Q1 = NPN-Transistor [part_number=2N2222A package="TO92 [THT]"]
  R4 = Resistor [tolerance=±5% resistance=150 package=THT]
  LED1 = LED - 3mm [color="Green (565nm)" part_number="Status LED" package="3 mm [THT]"]
  R5 = Resistor [tolerance=±5% resistance=150 package=THT]
  LED2 = LED - 3mm [color="Green (565nm)" part_number="Moist LED" package="3 mm [THT]"]
  R6 = Resistor [tolerance=±5% resistance=150 package=THT]
  LED3 = LED - 3mm [color="Green (565nm)" part_number="Comms LED" package="3 mm [THT]"]
  Q2 = Basic FET N-Channel [part_number=IRF540n package="TO220 [THT]"]
  M1 = DC Motor [part_number="Water Pump"]
  R7 = Resistor [tolerance=±5% resistance=1k package=THT]
  C1 = Electrolytic Capacitor [capacitance=1µF voltage=50V package="100 mil [THT, electrolytic]"]
  D1 = Rectifier Diode [part_number=1N4004 breakdown_voltage=3.6V package="300 mil [THT]"]
  R1 = Resistor [tolerance=±5% resistance=100 package=THT]
  S1 = Pushbutton [part_number="Debug switch" package="[THT]"]

nets:
  N1: Ethernet_Shield.GND, R3.Pin_1, R4.Pin_1, R5.Pin_1, R6.Pin_1, Q2.source, S1.Pin_1, S1.Pin_2
  N2: Ethernet_Shield.A0, R3.Pin_0, Q1.E
  N3: Ethernet_Shield.D2, R7.Pin_0
  N4: Ethernet_Shield.PWM_D3, S1.Pin_3, S1.Pin_4
  N5: Ethernet_Shield.SDCS, R1.Pin_1
  N6: Ethernet_Shield.PWM_D5, LED3.anode
  N7: Ethernet_Shield.PWM_D6, LED2.anode
  N8: Ethernet_Shield.D7, LED1.anode
  N9: Ethernet_Shield.5V, Q1.C
  N10: Ethernet_Shield.VIN, M1.pin_1, C1.+, D1.cathode
  GND: Q1.B, R1.Pin_0
  N11: R4.Pin_0, LED1.cathode
  N12: R5.Pin_0, LED2.cathode
  N13: R6.Pin_0, LED3.cathode
  N14: Q2.gate, R7.Pin_1
  N15: Q2.drain, M1.pin_2, C1.-, D1.anode

notes:
  Soil Probes
  Water Pump
